# Fritzing sketch RFID (saved by Fritzing 0.9.3b)
breadboards: 1

parts:
  LED1 = LED - 3mm [color="Red (633nm)" package="3 mm [THT]"]
  Componente1 = RFID-RC522-v3
  LED2 = LED - 3mm [color="Red (633nm)" package="3 mm [THT]"]
  Componente2 = Arduino Nano (Rev3.0) (ICSP)
  J1 = Piezo Speaker

nets:
  N1: LED1.cathode, Componente2.D6
  N2: LED1.anode, Componente1.GND, LED2.anode, J1.pin1
  N3: Componente1.SDA, Componente2.D10
  N4: Componente1.SCK, Componente2.D13/SCK
  N5: Componente1.MOSI, Componente2.D11/MOSI
  N6: Componente1.MISO, Componente2.D12/MISO
  N7: Componente1.RST, Componente2.D9
  3.3V: Componente1.3.3V, Componente2.3V3
  N8: LED2.cathode, Componente2.D7

custom parts:
  RFID-RC522-v3: A simple China made RFID-RC522 Reader (6x4 cm); do check the pin labels, as this is a MFRC522 based clone.
